# Fritzing sketch build_schematic_rev1 (saved by Fritzing 0.9.0b)
breadboards: 1

parts:
  RELAY_1 = RELAY-2 [package=relay-g5v]
  R1 = Resistor [tolerance=±5% resistance=1k package=THT]
  Q1 = NPN-Transistor [package="TO92 [THT]"]
  S1 = Toggle Switch [package=THT]
  U2 = 555 Timer [package="DIP8 [THT]"]
  C1 = Ceramic Capacitor [capacitance=0.01µF package="100 mil [THT, multilayer]"]
  R3 = Resistor [tolerance=±5% resistance=1k package=THT]
  C2 = Electrolytic Capacitor [capacitance=470µF package="100 mil [THT, electrolytic]"]
  R4 = Trimmer Potentiometer [maximum_resistance=10kΩ package=THT]
  Q2 = PNP-Transistor [package="TO92 [THT]"]
  R5 = Resistor [tolerance=±5% resistance=1k package=THT]
  R6 = Resistor [tolerance=±5% resistance=1k package=THT]
  R7 = Resistor [tolerance=±5% resistance=300 package=THT]
  J1_CONN = male pin header, 3 pins [form="♂ (male)"]
  J2_POWER_OUT = Screw terminal - 2 pins [package=THT]
  J1_POWER_IN = Screw terminal - 2 pins [package=THT]
  LED1 = LED - 5mm [color="Red (633nm)" package="5 mm [THT]"]
  R8 = Resistor [tolerance=±5% resistance=300 package=THT]

nets:
  N1: RELAY_1.2, R7.Pin_1
  N2: RELAY_1.5, J1_POWER_IN.pin1
  N3: RELAY_1.9, Q1.C, LED1.anode
  N4: RELAY_1.10, J2_POWER_OUT.pin2
  N5: R1.Pin_0, U2.Output
  N6: R1.Pin_1, Q1.B
  GND: Q1.E, U2.Ground, C1.0, C2.-, J1_CONN.pin1, R8.Pin_0
  3.3v: S1.COM, U2.Reset, U2.Vcc_Supply_Voltage, R4.leg2, Q2.E, J1_CONN.pin3
  N7: S1.L2, R7.Pin_0
  N8: U2.Trigger, R6.Pin_1
  N9: U2.Control_Voltage, C1.1
  N10: U2.Threshold, U2.Discharge, R3.Pin_1, C2.+
  N11: R3.Pin_0, R4.wiper
  N12: Q2.B, R5.Pin_1
  N13: Q2.C, R6.Pin_0
  N14: R5.Pin_0, J1_CONN.pin2
  N15: J2_POWER_OUT.pin1, J1_POWER_IN.pin2
  N16: LED1.cathode, R8.Pin_1

notes:
  Bamboo Build Status Alarm, A Raspberry Pi controlled relay that pulses a large alarm light., 1
  SIGNAL
