# Fritzing sketch build_schematic_rev2 (saved by Fritzing 0.9.0b)
circuit board: 5.04117cm x 4.29532cm
breadboards: 1

parts:
  Q1 = NPN-Transistor [package="TO92 [THT]"]
  PWR_OUT = Screw terminal - 2 pins [package=THT]
  PWR_IN = Screw terminal - 2 pins [package=THT]
  R1 = Resistor [tolerance=±5% resistance=1k package=THT]
  RELAY = RELAY-2 [package=relay-g5v]
  CTRL = male pin header, 3 pins [form="♂ (male)"]
  D1 = Rectifier Diode [part_number=1N4001 package="300 mil [THT]"]
  R2 = Resistor [tolerance=±5% resistance=300 package=THT]
  S_PWR = male pin header, 2 pins [form="♂ (male)"]
  LEDS = male pin header, 3 pins [form="♂ (male)"]
  R3 = Resistor [tolerance=±5% resistance=1k package=THT]
  S_MAN = Pushbutton [package="[THT]"]

nets (from the schematic view):
  GND: Q1.E, CTRL.pin2, R2.Pin_0
  N1: Q1.B, R3.Pin_1
  N2: Q1.C, R1.Pin_0, D1.cathode
  N3: PWR_OUT.pin1, PWR_IN.pin2
  N4: PWR_OUT.pin2, RELAY.5
  N5: PWR_IN.pin1, RELAY.1
  N6: R1.Pin_1, LEDS.pin1
  N7: RELAY.2, S_PWR.pin2, LEDS.pin3, S_MAN.Pin_3, S_MAN.Pin_4
  N8: RELAY.9, D1.anode
  N9: CTRL.pin1, R3.Pin_0, S_MAN.Pin_1, S_MAN.Pin_2
  N10: CTRL.pin3, S_PWR.pin1
  N11: R2.Pin_1, LEDS.pin2

notes:
  BIGBANK
  Build Monitor
  A. Roots
  rev 2
  Bamboo Build Status Alarm, A Raspberry Pi controlled relay that pulses a large alarm light., 2
